// Logisim project Logisim.circ as structural Verilog: 1 circuit, main circuit main
module main (
  input  RESET,
  input  MOVE,
  input  EAT,
  input  HIT,
  input  PAUSE,
  input  RESET_2,
  output MOVE_2,
  output NEWFOOD,
  output GROW,
  output GameOver,
  output GameStop
);

  wire and_1_out, and_2_out, and_3_out, and_4_out, and_5_out, and_6_out, and_7_out, and_8_out, and_9_out,
       and_10_out, and_11_out, clock_1_out, not_1_out, not_2_out, not_3_out, not_4_out, not_5_out, not_6_out,
       not_7_out, not_8_out, not_9_out, not_10_out, not_11_out, not_12_out, not_13_out, not_14_out,
       not_15_out, not_16_out, not_17_out, not_18_out, not_19_out, not_20_out, not_21_out, not_22_out,
       not_23_out, not_24_out, not_25_out, not_26_out, not_27_out, not_28_out, not_29_out, not_30_out,
       or_1_out, or_2_out, or_3_out, or_4_out, or_5_out, register_1_q, register_2_q, register_3_q, xor_1_out,
       xor_2_out;

  not not_1 (not_1_out, register_1_q);
  not not_2 (not_2_out, register_2_q);
  not not_3 (not_3_out, register_3_q);
  not not_4 (not_4_out, register_2_q);
  not not_5 (not_5_out, register_3_q);
  not not_6 (not_6_out, EAT);
  not not_7 (not_7_out, HIT);
  not not_8 (not_8_out, PAUSE);
  not not_9 (not_9_out, register_1_q);
  not not_10 (not_10_out, PAUSE);
  xor xor_1 (xor_1_out, register_2_q, register_3_q);
  not not_11 (not_11_out, register_2_q);
  not not_12 (not_12_out, register_3_q);
  not not_13 (not_13_out, PAUSE);
  or or_1 (or_1_out, EAT, HIT);
  not not_14 (not_14_out, register_1_q);
  not not_15 (not_15_out, register_2_q);
  not not_16 (not_16_out, register_3_q);
  or or_2 (or_2_out, HIT, PAUSE);
  not not_17 (not_17_out, register_1_q);
  xor xor_2 (xor_2_out, register_2_q, register_3_q);
  not not_18 (not_18_out, register_1_q);
  and and_1 (and_1_out, not_1_out, not_2_out, not_3_out, MOVE);
  and and_2 (and_2_out, register_1_q, not_4_out, not_5_out, not_6_out, not_7_out, not_8_out);
  and and_3 (and_3_out, not_9_out, not_10_out, xor_1_out);
  and and_4 (and_4_out, register_1_q, not_11_out, not_12_out, not_13_out, or_1_out);
  and and_5 (and_5_out, not_14_out, register_2_q, register_3_q);
  and and_6 (and_6_out, register_1_q, not_15_out, not_16_out, or_2_out);
  and and_7 (and_7_out, not_17_out, PAUSE, xor_2_out);
  and and_8 (and_8_out, not_18_out, register_2_q, register_3_q);
  not not_19 (not_19_out, RESET);
  and and_9 (and_9_out, not_19_out, or_3_out);
  or or_3 (or_3_out, and_1_out, and_2_out, and_3_out);
  not not_20 (not_20_out, RESET);
  and and_10 (and_10_out, not_20_out, or_4_out);
  or or_4 (or_4_out, and_4_out, and_5_out);
  not not_21 (not_21_out, RESET);
  and and_11 (and_11_out, not_21_out, or_5_out);
  or or_5 (or_5_out, and_6_out, and_7_out, and_8_out);
  Clock clock_1 (.out(clock_1_out));
  Register #(.width(1)) register_1 (.D(and_9_out), .Q(register_1_q), .clk(clock_1_out), .clr(RESET_2));  // open: en
  Register #(.width(1)) register_2 (.D(and_10_out), .Q(register_2_q), .clk(clock_1_out), .clr(RESET_2));  // open: en
  Register #(.width(1)) register_3 (.D(and_11_out), .Q(register_3_q), .clk(clock_1_out), .clr(RESET_2));  // open: en
  not not_22 (not_22_out, register_2_q);
  not not_23 (not_23_out, register_3_q);
  not not_24 (not_24_out, register_1_q);
  not not_25 (not_25_out, register_3_q);
  not not_26 (not_26_out, register_1_q);
  not not_27 (not_27_out, register_3_q);
  not not_28 (not_28_out, register_1_q);
  not not_29 (not_29_out, register_1_q);
  not not_30 (not_30_out, register_2_q);
  and and_12 (MOVE_2, register_1_q, not_22_out, not_23_out);
  and and_13 (NEWFOOD, not_24_out, register_2_q, not_25_out);
  and and_14 (GROW, not_26_out, register_2_q, not_27_out);
  and and_15 (GameOver, not_28_out, register_2_q, register_3_q);
  and and_16 (GameStop, not_29_out, not_30_out, register_3_q);

  // Notes on the sheet:
  //   S2_next
  //   S1_next
  //   S0_next
  //   S2
  //   S1
  //   S0
endmodule
